// Logisim project ARA_SoSe_25_Schaltungen.circ as structural Verilog
module _2_1_Multiplexer__Kap__2__S__68 (
  input  e0,
  input  sel,
  input  e1,
  output f
);

  wire and_1_out, and_2_out;

  and and_1 (and_1_out, e0, ~sel);  // AND_Gate
  and and_2 (and_2_out, sel, e1);
  or or_1 (f, and_1_out, and_2_out);
endmodule

module _1_2_Demultiplexer__Kap__2__S__70 (
  input  e,
  input  sel,
  output f0,
  output f1
);

  or or_1 (f0, e, sel);
  or or_2 (f1, e, ~sel);  // OR_Gate
endmodule

module \_3_Bit_Identitäts_Komparator__Kap__2__S_78  (
  input  x1,
  input  y1,
  input  x2,
  input  y2,
  input  x3,
  input  y3,
  output f
);

  wire xnor_1_out, xnor_2_out, xnor_3_out;

  xnor xnor_1 (xnor_1_out, x1, y1);
  xnor xnor_2 (xnor_2_out, x2, y2);
  xnor xnor_3 (xnor_3_out, x3, y3);
  and and_1 (f, xnor_1_out, xnor_2_out, xnor_3_out);
endmodule

module \_1_Bit_Größen_Komparator__Kap__2__S__79  (
  input  x,
  input  y,
  output x_y,
  output x_y_2,
  output x_y_3
);

  and and_1 (x_y, x, ~y);  // AND_Gate
  and and_2 (x_y_3, ~x, y);  // AND_Gate
  nor nor_1 (x_y_2, x_y, x_y_3);
endmodule

module Halbaddierer__Kap__2__S__80 (
  input  a,
  input  b,
  output S,
  output C
);

  wire and_1_out, and_2_out;

  and and_1 (and_1_out, a, ~b);  // AND_Gate
  and and_2 (and_2_out, ~a, b);  // AND_Gate
  and and_3 (C, a, b);
  or or_1 (S, and_1_out, and_2_out);
endmodule

module Volladdierer__Kap__2__S__81 (
  input  a,
  input  b,
  input  c,
  output C_2,
  output S
);

  wire halbaddierer_kap_2_s_80_1_c, halbaddierer_kap_2_s_80_1_s, halbaddierer_kap_2_s_80_2_c;

  or or_1 (C_2, halbaddierer_kap_2_s_80_1_c, halbaddierer_kap_2_s_80_2_c);
  Halbaddierer__Kap__2__S__80 halbaddierer_kap_2_s_80_1 (
    .a(a), .b(b), .S(halbaddierer_kap_2_s_80_1_s), .C(halbaddierer_kap_2_s_80_1_c));
  Halbaddierer__Kap__2__S__80 halbaddierer_kap_2_s_80_2 (
    .a(halbaddierer_kap_2_s_80_1_s), .b(c), .S(S), .C(halbaddierer_kap_2_s_80_2_c));
endmodule

module Ripple_Carry_Addierer__Kap__2__S__82 (
  input  a3,
  input  a2,
  input  a1,
  input  a0,
  input  b3,
  input  b2,
  input  b1,
  input  b0,
  output S4,
  output S3,
  output S2,
  output S1,
  output S0
);

  wire halbaddierer_kap_2_s_80_1_c, volladdierer_kap_2_s_81_2_c_2, volladdierer_kap_2_s_81_3_c_2;

  Volladdierer__Kap__2__S__81 volladdierer_kap_2_s_81_1 (
    .a(a3), .b(b3), .c(volladdierer_kap_2_s_81_2_c_2), .C_2(S4), .S(S3));
  Volladdierer__Kap__2__S__81 volladdierer_kap_2_s_81_2 (
    .a(a2), .b(b2), .c(volladdierer_kap_2_s_81_3_c_2), .C_2(volladdierer_kap_2_s_81_2_c_2), .S(S2));
  Volladdierer__Kap__2__S__81 volladdierer_kap_2_s_81_3 (
    .a(a1), .b(b1), .c(halbaddierer_kap_2_s_80_1_c), .C_2(volladdierer_kap_2_s_81_3_c_2), .S(S1));
  Halbaddierer__Kap__2__S__80 halbaddierer_kap_2_s_80_1 (.a(a0), .b(b0), .S(S0), .C(halbaddierer_kap_2_s_80_1_c));
endmodule

module Addierer_Subtrahierer__Kap__2__S__85 (
  input  a3,
  input  a2,
  input  a1,
  input  a0,
  input  b3,
  input  b2,
  input  b1,
  input  b0,
  input  _0___ADD,
  output S4,
  output S3,
  output S2,
  output S1,
  output S0
);

  wire n2_1_multiplexer_kap_2_s_68_1_f, n2_1_multiplexer_kap_2_s_68_2_f, n2_1_multiplexer_kap_2_s_68_3_f,
       n2_1_multiplexer_kap_2_s_68_4_f, not_1_out, not_2_out, not_3_out, not_4_out,
       volladdierer_kap_2_s_81_2_c_2, volladdierer_kap_2_s_81_3_c_2, volladdierer_kap_2_s_81_4_c_2;

  not not_1 (not_1_out, b3);
  _2_1_Multiplexer__Kap__2__S__68 u_2_1_multiplexer_kap_2_s_68_1 (
    .e0(b3), .sel(_0___ADD), .e1(not_1_out), .f(n2_1_multiplexer_kap_2_s_68_1_f));
  Volladdierer__Kap__2__S__81 volladdierer_kap_2_s_81_1 (
    .a(a3), .b(n2_1_multiplexer_kap_2_s_68_1_f), .c(volladdierer_kap_2_s_81_2_c_2), .C_2(S4), .S(S3));
  not not_2 (not_2_out, b2);
  _2_1_Multiplexer__Kap__2__S__68 u_2_1_multiplexer_kap_2_s_68_2 (
    .e0(b2), .sel(_0___ADD), .e1(not_2_out), .f(n2_1_multiplexer_kap_2_s_68_2_f));
  Volladdierer__Kap__2__S__81 volladdierer_kap_2_s_81_2 (
    .a(a2), .b(n2_1_multiplexer_kap_2_s_68_2_f), .c(volladdierer_kap_2_s_81_3_c_2),
    .C_2(volladdierer_kap_2_s_81_2_c_2), .S(S2));
  not not_3 (not_3_out, b1);
  _2_1_Multiplexer__Kap__2__S__68 u_2_1_multiplexer_kap_2_s_68_3 (
    .e0(b1), .sel(_0___ADD), .e1(not_3_out), .f(n2_1_multiplexer_kap_2_s_68_3_f));
  Volladdierer__Kap__2__S__81 volladdierer_kap_2_s_81_3 (
    .a(a1), .b(n2_1_multiplexer_kap_2_s_68_3_f), .c(volladdierer_kap_2_s_81_4_c_2),
    .C_2(volladdierer_kap_2_s_81_3_c_2), .S(S1));
  not not_4 (not_4_out, b0);
  _2_1_Multiplexer__Kap__2__S__68 u_2_1_multiplexer_kap_2_s_68_4 (
    .e0(b0), .sel(_0___ADD), .e1(not_4_out), .f(n2_1_multiplexer_kap_2_s_68_4_f));
  Volladdierer__Kap__2__S__81 volladdierer_kap_2_s_81_4 (
    .a(a0), .b(n2_1_multiplexer_kap_2_s_68_4_f), .c(_0___ADD), .C_2(volladdierer_kap_2_s_81_4_c_2), .S(S0));

  // Notes on the sheet:
  //   1 = SUB
endmodule
